# Fritzing sketch sensordata_diagram (saved by Fritzing 0.9.4)
breadboards: 1

parts:
  Part1 = Arduino Uno (Rev3)
  HC-SR04_Sensor_1 = HC-SR04 Ultrasonic Distance Sensor
  Part2 = InvenSense MPU6050

nets:
  N1: Part1.D9_PWM, HC-SR04_Sensor_1.TRIG
  N2: Part1.D10_PWM/SS, HC-SR04_Sensor_1.ECHO
  N3: Part1.A4/SDA, Part2.SDA
  N4: Part1.A5/SCL, Part2.SCL
  VCC: Part1.5V, HC-SR04_Sensor_1.VCC, Part2.VCC
  GND: Part1.GND, HC-SR04_Sensor_1.GND, Part2.GND
